// Logisim project DDCA project 2.circ as structural Verilog: 1 circuit, main circuit main
module main (
  input  G3,
  input  G2,
  input  G1,
  input  G0,
  output B1,
  output B2,
  output B0,
  output B3
);

  xor xor_1 (B1, G0, G1);
  xor xor_2 (B2, G1, G2);
  xor xor_3 (B0, G2, G3);

  assign B3 = G3;
endmodule
